// Logisim project projet_etu.circ as structural Verilog: 11 circuits, main circuit main
module main (
  input  Reset,
  input  ResetRAM
);

  wire call, Clock, Clock_out, Cond, CTRL, Exec, Fetch, getcst_1_imm, Load, ramctrl_1_memload,
       ramctrl_1_memstore, ret, Store, WriteReg;
  wire [2:0] GetOp;
  wire [15:0] Addr, ALU_OUT, getcst_1_cst, JMP_Address, MemIN, multiplexer_1_out, PC, R0, R1, R2, R3, R4, R5,
       R6, R7, SRC1, SRC2;
  wire [31:0] bit_extender_1_out, IR, MemOUT;

  Clock u_Clock (.out(Clock_out));
  Seq seq_1 (.ClockOrig(Clock_out), .reset(Reset), .Fetch(Fetch), .Exec(Exec), .Clock(Clock));
  LED led_1 (.in(Clock_out));
  RegPC regpc_1 (
    .JMP_Address(JMP_Address), .Cond(Cond), .CTRL(CTRL), .Clock(Exec), .Reset(Reset), .PC(PC), .CALL(call),
    .RET(ret));
  // Probe on PC
  GetAddr getaddr_1 (.PC(PC), .Addr(Addr), .Fetch(Fetch), .Load(Load), .Store(Store), .SRC1(SRC1));
  // Probe on Addr
  LED led_2 (.in(Fetch));
  LED led_3 (.in(Exec));
  // Probe on MemIN
  assign bit_extender_1_out = {{16{MemIN[15]}}, MemIN};  // Bit_Extender bit_extender_1
  // Probe on PC
  // Probe on IR
  RamCtrl ramctrl_1 (
    .Store(Store), .Fetch(Fetch), .Exec(Exec), .Load(Load), .MemStore(ramctrl_1_memstore),
    .MemLoad(ramctrl_1_memload), .Clock(Clock));
  CTRL ctrl_1 (.SRC1(SRC1), .SRC2(SRC2), .CodeOperation(GetOp), .CTRL(CTRL), .Condition(Cond), .call(call), .ret(ret));
  LED LD (.in(Load));
  LED led_4 (.in(CTRL));
  RAM #(.addrWidth(16), .dataWidth(32), .bus("separate")) ram_1 (
    .addr(Addr), .din(bit_extender_1_out), .data(MemOUT), .str(ramctrl_1_memstore), .clk(ramctrl_1_memstore),
    .ld(ramctrl_1_memload), .clr(ResetRAM));  // open: sel
  // Probe on R0
  // Probe on R3
  // Probe on R6
  LED STR (.in(Store));
  DecodeIR decodeir_1 (
    .IR(IR), .GetOp(GetOp), .JMPAddress(JMP_Address), .WriteReg(WriteReg), .CTRL(CTRL), .Store(Store),
    .Load(Load));
  // Probe on R1
  // Probe on R4
  // Probe on R7
  // Probe on MemOUT
  Register #(.width(32), .trigger("falling")) RegIR (.D(MemOUT), .Q(IR), .clk(Fetch), .clr(Reset));  // open: en
  // Probe on R2
  // Probe on R5
  // Probe on IR
  // Probe on MemOUT[15:0]
  // Probe on IR[8:6]
  // Probe on IR[11:9]
  // Probe on IR[14:12]
  // Probe on getcst_1_cst
  GetCst getcst_1 (.IR(IR), .Cst(getcst_1_cst), .Imm(getcst_1_imm));
  Multiplexer #(.width(16), .disabled(0)) multiplexer_1 (
    .in0(ALU_OUT), .in1(MemOUT[15:0]), .out(multiplexer_1_out), .sel(Load));  // open: en
  Registres registres_1 (
    .SR1(IR[11:9]), .IN(multiplexer_1_out), .SR2(IR[14:12]), .OUT_SR1(SRC1), .OUT_SR2(SRC2), .OUT_DR(MemIN),
    .R0(R0), .R1(R1), .R2(R2), .R3(R3), .R4(R4), .R5(R5), .R6(R6), .R7(R7), .Reset(Reset), .Clock(Exec),
    .WriteReg(WriteReg), .DR(IR[8:6]));
  // Probe on SRC1
  ALU alu_1 (.Imm(getcst_1_imm), .e2(GetOp), .Input1(SRC1), .Input2(SRC2), .Cst(getcst_1_cst), .Output(ALU_OUT));
  // Probe on GetOp
  // Probe on multiplexer_1_out
  // Probe on SRC2
  // Probe on R0
  // Probe on R1
  // Probe on R2
  // Probe on R3
  // Probe on R4
  // Probe on R5
  // Probe on R6
  // Probe on R7
  // Probe on ALU_OUT

  // Notes on the sheet:
  //   régulation PC
  //   RAM
  //   constante = 16 derniers bits
endmodule

module ALU (
  input  [15:0] Input2,
  input  [15:0] Cst,
  input  Imm,
  input  [15:0] Input1,
  input  [2:0] e2,
  output [15:0] Output
);

  wire comparator_1_eq, not_1_out;
  wire [15:0] adder_1_out, and_1_out, IN2, multiplier_1_out, or_1_out, shifter_1_out, shifter_2_out, SL, SR,
       subtractor_1_out, xor_1_out;

  Multiplexer #(.width(16), .enable("false")) multiplexer_1 (.in0(Input2), .in1(Cst), .out(IN2), .sel(Imm));
  Multiplier #(.width(16)) multiplier_1 (.a(IN2), .b(Input1), .out(multiplier_1_out));  // open: cin, cout
  assign xor_1_out = IN2 ^ Input1;  // XOR_Gate xor_1, 16 bits wide
  assign or_1_out = IN2 | Input1;  // OR_Gate or_1, 16 bits wide
  assign and_1_out = IN2 & Input1;  // AND_Gate and_1, 16 bits wide
  Subtractor #(.width(16)) subtractor_1 (.a(Input1), .b(IN2), .out(subtractor_1_out));  // open: bin, bout
  Adder #(.width(16)) adder_1 (.a(IN2), .b(Input1), .out(adder_1_out));  // open: cin, cout
  Multiplexer #(.select(3), .width(16), .enable("false")) multiplexer_2 (
    .in0(multiplier_1_out), .in1(SR), .in2(SL), .in3(xor_1_out), .in4(or_1_out), .in5(and_1_out),
    .in6(subtractor_1_out), .in7(adder_1_out), .out(Output), .sel(e2));
  Shifter #(.width(16), .shift("lr")) shifter_1 (.in(Input1), .\dist (IN2[3:0]), .out(shifter_1_out));
  Shifter #(.width(16)) shifter_2 (.in(Input1), .\dist (IN2[3:0]), .out(shifter_2_out));
  Comparator #(.width(12)) comparator_1 (.a(IN2[15:4]), .b({12{1'b0}}), .eq(comparator_1_eq));  // open: gt, lt
  not not_1 (not_1_out, comparator_1_eq);
  Multiplexer #(.width(16), .enable("false")) multiplexer_3 (
    .in0(shifter_1_out), .in1({16{1'b0}}), .out(SR), .sel(not_1_out));
  Multiplexer #(.width(16), .enable("false")) multiplexer_4 (
    .in0(shifter_2_out), .in1({16{1'b0}}), .out(SL), .sel(not_1_out));

  // Other names for the same wires on the sheet: IN1[15:0] = Input1
endmodule

module DecodeIR (
  input  [31:0] IR,
  output WriteReg,
  output Load,
  output Store,
  output CTRL,
  output [2:0] GetOp,
  output [15:0] JMPAddress
);

  wire and_1_out, demultiplexer_1_out0, demultiplexer_1_out1, demultiplexer_1_out2, not_1_out;

  Demultiplexer #(.select(2), .disabled(0)) demultiplexer_1 (
    .out0(demultiplexer_1_out0), .out1(demultiplexer_1_out1), .out2(demultiplexer_1_out2), .out3(CTRL),
    .in(1'b1), .sel(IR[1:0]));  // open: en
  or or_1 (WriteReg, demultiplexer_1_out0, and_1_out);
  and and_1 (and_1_out, demultiplexer_1_out1, IR[2]);
  and and_2 (Load, IR[2], demultiplexer_1_out1);
  and and_3 (Store, demultiplexer_1_out1, not_1_out);
  not not_1 (not_1_out, IR[2]);

  assign GetOp = IR[4:2];
  assign JMPAddress = IR[31:16];

  // Notes on the sheet:
  //   dans le cas d'un JMP, l'adresse à laquelle on va.
  //   si on charge un truc dans un registre
  //   explicite
  //   si on JMP. Cotnrole des instructions
endmodule

module GetAddr (
  input  [15:0] PC,
  input  [15:0] SRC1,
  input  Fetch,
  input  Store,
  input  Load,
  output [15:0] Addr
);

  wire and_1_out, not_1_out, or_1_out;

  not not_1 (not_1_out, Fetch);
  or or_1 (or_1_out, Store, Load);
  Multiplexer #(.width(16), .disabled(0)) multiplexer_1 (
    .in0(PC), .in1(SRC1), .out(Addr), .sel(and_1_out));  // open: en
  and and_1 (and_1_out, not_1_out, or_1_out);

  // Notes on the sheet:
  //   dans tt les cas, l'adresse arrive par src1
  //   (quand on load ou qu'on store)
endmodule

module GetCst (
  input  [31:0] IR,
  output [15:0] Cst,
  output Imm
);


  assign Cst = IR[31:16];
  assign Imm = IR[5];
endmodule

module RamCtrl (
  input  Clock,
  input  Exec,
  input  Fetch,
  input  Load,
  input  Store,
  output MemLoad,
  output MemStore
);

  wire and_1_out;

  and and_1 (and_1_out, Exec, Load);
  and and_2 (MemStore, Exec, Clock, Store);
  or or_1 (MemLoad, Fetch, and_1_out);
endmodule

module Registres (
  input  [15:0] IN,
  input  [2:0] SR1,
  input  WriteReg,
  input  [2:0] DR,
  input  [2:0] SR2,
  input  Clock,
  input  Reset,
  output [15:0] R0,
  output [15:0] OUT_SR1,
  output [15:0] R1,
  output [15:0] R2,
  output [15:0] R3,
  output [15:0] R4,
  output [15:0] R5,
  output [15:0] OUT_SR2,
  output [15:0] OUT_DR,
  output [15:0] R6,
  output [15:0] R7
);

  wire demultiplexer_1_out0, demultiplexer_1_out1, demultiplexer_1_out2, demultiplexer_1_out3,
       demultiplexer_1_out4, demultiplexer_1_out5, demultiplexer_1_out6, demultiplexer_1_out7;

  Demultiplexer #(.select(3), .disabled(0)) demultiplexer_1 (
    .out0(demultiplexer_1_out0), .out1(demultiplexer_1_out1), .out2(demultiplexer_1_out2),
    .out3(demultiplexer_1_out3), .out4(demultiplexer_1_out4), .out5(demultiplexer_1_out5),
    .out6(demultiplexer_1_out6), .out7(demultiplexer_1_out7), .in(1'b1), .sel(DR), .en(WriteReg));
  Register #(.width(16), .trigger("falling")) u_R0 (
    .D(IN), .en(demultiplexer_1_out0), .Q(R0), .clk(Clock), .clr(Reset));
  Register #(.width(16), .trigger("falling")) u_R1 (
    .D(IN), .en(demultiplexer_1_out1), .Q(R1), .clk(Clock), .clr(Reset));
  Register #(.width(16), .trigger("falling")) u_R2 (
    .D(IN), .en(demultiplexer_1_out2), .Q(R2), .clk(Clock), .clr(Reset));
  Register #(.width(16), .trigger("falling")) u_R3 (
    .D(IN), .en(demultiplexer_1_out3), .Q(R3), .clk(Clock), .clr(Reset));
  Register #(.width(16), .trigger("falling")) u_R4 (
    .D(IN), .en(demultiplexer_1_out4), .Q(R4), .clk(Clock), .clr(Reset));
  Register #(.width(16), .trigger("falling")) u_R5 (
    .D(IN), .en(demultiplexer_1_out5), .Q(R5), .clk(Clock), .clr(Reset));
  Register #(.width(16), .trigger("falling")) u_R6 (
    .D(IN), .en(demultiplexer_1_out6), .Q(R6), .clk(Clock), .clr(Reset));
  Register #(.width(16), .trigger("falling")) u_R7 (
    .D(IN), .en(demultiplexer_1_out7), .Q(R7), .clk(Clock), .clr(Reset));
  Multiplexer #(.select(3), .width(16), .enable("false")) multiplexer_1 (
    .in0(R0), .in1(R1), .in2(R2), .in3(R3), .in4(R4), .in5(R5), .in6(R6), .in7(R7), .out(OUT_SR1), .sel(SR1));
  Multiplexer #(.select(3), .width(16), .enable("false")) multiplexer_2 (
    .in0(R0), .in1(R1), .in2(R2), .in3(R3), .in4(R4), .in5(R5), .in6(R6), .in7(R7), .out(OUT_DR), .sel(SR2));

  assign OUT_SR2 = OUT_DR;

  // Notes on the sheet:
  //   DR c'est ce qu'on met dans la mémoire
  //   OR, si on met qlqchose dans celle ci, ce sera SR2 par construction
endmodule

module RegPC (
  input  CALL,
  input  RET,
  input  [15:0] JMP_Address,
  input  Cond,
  input  CTRL,
  input  Clock,
  input  Reset,
  output [15:0] PC
);

  wire and_1_out, not_1_out;
  wire [15:0] adder_1_out, current_ADress, multiplexer_1_out, multiplexer_2_out, pile_1_return_adress;

  Pile pile_1 (
    .RET(RET), .Call(CALL), .clock(Clock), .Reset(Reset), .current_adress(current_ADress),
    .Return_Adress(pile_1_return_adress));
  Multiplexer #(.width(16)) multiplexer_1 (
    .in0(adder_1_out), .in1(pile_1_return_adress), .out(multiplexer_1_out), .sel(RET));  // open: en
  and and_1 (and_1_out, Cond, CTRL);
  Multiplexer #(.width(16)) multiplexer_2 (
    .in0(multiplexer_1_out), .in1(JMP_Address), .out(multiplexer_2_out), .sel(and_1_out));  // open: en
  Register #(.width(16), .trigger("falling")) u_PC (
    .D(multiplexer_2_out), .Q(PC), .clk(Clock), .clr(Reset));  // open: en
  Adder #(.width(16)) adder_1 (.a(16'h1), .b(PC), .out(adder_1_out));  // open: cin, cout
  Register #(.width(16), .trigger("falling")) tempPC (
    .D(PC), .Q(current_ADress), .clk(not_1_out), .clr(Reset));  // open: en
  not not_1 (not_1_out, Clock);

  // Notes on the sheet:
  //   adresse
  //   à chaque tik, PC augmente de 1 (on passe à la seconde ligne du prog, etc...
  //   CEPANDANNNNT, si il y a  une opération de CTRL et qu'elle réussie, on saute. sinon, on fait +1.
  //   et si on a une opé call/ret, on court-circuite le circuit classique
  //   s
endmodule

module Seq (
  input  ClockOrig,
  input  reset,
  output Fetch,
  output Exec,
  output Clock
);

  Register #(.width(1), .trigger("falling")) register_1 (
    .D(Fetch), .Q(Exec), .clk(ClockOrig), .clr(reset));  // open: en
  not not_1 (Fetch, Exec);
  buf buffer_1 (Clock, ClockOrig);
endmodule

module CTRL (
  input  [15:0] SRC1,
  input  [15:0] SRC2,
  input  [2:0] CodeOperation,
  input  CTRL,
  output Condition,
  output call,
  output ret
);

  wire comparator_1_eq, comparator_1_gt, comparator_1_lt, comparator_2_eq, comparator_3_eq, not_1_out;

  Comparator #(.width(16)) comparator_1 (
    .a(SRC1), .b(SRC2), .gt(comparator_1_gt), .eq(comparator_1_eq), .lt(comparator_1_lt));
  not not_1 (not_1_out, comparator_1_eq);
  Multiplexer #(.select(3), .disabled(0)) multiplexer_1 (
    .in0(1'b1), .in1(comparator_1_eq), .in2(not_1_out), .in3(comparator_1_gt), .in4(comparator_1_lt),
    .in5(1'b1), .in6(1'b0), .out(Condition), .sel(CodeOperation), .en(CTRL));  // open: in7
  Comparator #(.width(3)) comparator_2 (.a(3'b101), .b(CodeOperation), .eq(comparator_2_eq));  // open: gt, lt
  Comparator #(.width(3)) comparator_3 (.a(CodeOperation), .b(3'b110), .eq(comparator_3_eq));  // open: gt, lt
  and and_1 (call, CTRL, comparator_2_eq);
  and and_2 (ret, comparator_3_eq, CTRL);

  // Notes on the sheet:
  //   call ~ JMP => cond= 1
endmodule

module Pile (
  input  RET,
  input  Call,
  input  clock,
  input  Reset,
  input  [15:0] current_adress,
  output [15:0] Return_Adress
);

  wire or_1_out;
  wire [15:0] adder_1_out, multiplexer_1_out, multiplexer_2_out, ram_1_data, register_1_q, subtractor_1_out;

  Multiplexer #(.width(16)) multiplexer_1 (
    .in0(adder_1_out), .in1(subtractor_1_out), .out(multiplexer_1_out), .sel(RET));  // open: en
  or or_1 (or_1_out, RET, Call);
  Register #(.width(16)) register_1 (.D(multiplexer_1_out), .en(or_1_out), .Q(register_1_q), .clk(clock), .clr(Reset));
  Subtractor #(.width(16)) subtractor_1 (.a(register_1_q), .b(16'h1), .out(subtractor_1_out));  // open: bin, bout
  Adder #(.width(16)) adder_1 (.a(register_1_q), .b(16'h1), .out(adder_1_out));  // open: cin, cout
  Multiplexer #(.width(16)) multiplexer_2 (
    .in0(subtractor_1_out), .in1(register_1_q), .out(multiplexer_2_out), .sel(Call));  // open: en
  RAM #(.addrWidth(16), .dataWidth(16), .bus("separate")) ram_1 (
    .addr(multiplexer_2_out), .din(current_adress), .data(ram_1_data), .str(Call), .sel(or_1_out),
    .clk(clock), .ld(RET), .clr(Reset));
  Adder #(.width(16)) adder_2 (.a(ram_1_data), .b(16'h1), .out(Return_Adress));  // open: cin, cout
endmodule
